# Fritzing sketch atari-600xl-pbi-nolevel (saved by Fritzing 0.9.3b)
circuit board: 9.323cm x 6.91762cm
breadboards: 1

parts:
  LEVELSHT = Adafruit 4-channel I2C-safe Bi-directional Logic Level Converter [part_number="Adafruit #757"]
  U1 = ESP32-38PinWide [part_number=ESP32-38PinWide]
  R1 = Resistor [tolerance=±5% resistance=10k package=THT]
  MIC = Breakout Board for Electret Microphone
  J1 = shrouded pin header, 50 pins [form="♂ (shrouded male)"]
  R2 = Resistor [tolerance=±5% resistance=10k package=THT]
  R3 = Resistor [tolerance=±5% resistance=220 package=THT]

nets:
  GND: LEVELSHT.GND, U1.GND, MIC.GND, J1.pin1, J1.pin10, J1.pin15, J1.pin26, J1.pin30, J1.pin35, J1.pin36, R2.Pin_1
  ESP_IRQ: LEVELSHT.A4, U1.GPIO22
  ESP_RDY: LEVELSHT.A3, U1.GPIO1
  ESP_ES: LEVELSHT.A2, U1.GPIO3
  ESP_MPD: LEVELSHT.A1, U1.GPIO21
  3.3V: LEVELSHT.LV, U1.3.3, MIC.VCC
  MPD_I: LEVELSHT.B4, J1.pin22
  ES_I: LEVELSHT.B3, J1.pin50
  RDY_I: LEVELSHT.B2, J1.pin33
  IRQ_I: LEVELSHT.B1, J1.pin18
  5V: LEVELSHT.HV, U1.VIN, J1.pin24, J1.pin27
  N1: U1.EN, R1.Pin_1, R2.Pin_0
  PH2_O: U1.GPIO36, J1.pin16
  RW_O: U1.GPIO39, J1.pin28
  REF_O: U1.GPIO34, J1.pin31
  D7_IO: U1.GPIO35, J1.pin37
  D5_IO: U1.GPIO32, J1.pin38
  D3_IO: U1.GPIO33, J1.pin39
  D1_IO: U1.GPIO25, J1.pin40
  A15_O: U1.GPIO26, J1.pin41
  A14_O: U1.GPIO27, J1.pin42
  A12_O: U1.GPIO14, J1.pin43
  A10_O: U1.GPIO12, J1.pin44
  A8_O: U1.GPIO13, J1.pin45
  A5_O: U1.GPIO9, J1.pin47
  A3_O: U1.GPIO10, J1.pin48
  A1_O: U1.GPIO11, J1.pin49
  A0_O: U1.GPIO6, J1.pin2
  A2_0: U1.GPIO7, J1.pin3
  A4_O: U1.GPIO8, J1.pin4
  A6_O: U1.GPIO15, J1.pin5
  A7_O: U1.GPIO2, J1.pin6
  A9_O: U1.GPIO0, J1.pin7
  A11_O: U1.GPIO4, J1.pin8
  A13_O: U1.GPIO16, J1.pin9
  D0_IO: U1.GPIO17, J1.pin11
  D2_IO: U1.GPIO5, J1.pin12
  D4_IO: U1.GPIO18, J1.pin13
  D6_IO: U1.GPIO19, J1.pin14
  ESP_MIC: U1.GPIO23, R3.Pin_1
  RST_O: R1.Pin_0, J1.pin34
  N2: MIC.AUD, R3.Pin_0
  NOT CONNECTED 1: J1.pin17
  NOT CONNECTED 2: J1.pin19
  NOT CONNECTED 3: J1.pin20
  CAS_O: J1.pin21
  UNUSED GND 1: J1.pin23
  AUD_I: J1.pin25
  RAS_O: J1.pin29
  CASINH_O: J1.pin32
  UNUSED GND 2: J1.pin46

notes:
  1) https://www.amazon.com/Connector-40p-98-Finger-Through-Durable/dp/B09MZXJ8Q3/ref=sr_1_15?crid=XJIJ1S8Y0NPS&keywords=edge%2Bconnector%2B0.1%2Binches&qid=1644340803&sprefix=edge%2Bconnector%2B0.1%2Binches%2Caps%2C406&sr=8-15&th=1
  2) https://www.amazon.com/HiLetgo-ESP-WROOM-32-Development-Microcontroller-Integrated/dp/B0718T232Z/ref=sr_1_10?keywords=ESP32+38+pin&qid=1644360022&sr=8-10
  3) https://www.amazon.com/KeeYees-Channels-Converter-Bi-Directional-Shifter/dp/B07LG646VS/ref=sr_1_3?keywords=4-channel+I2C-safe+Bi-directional+Logic+Level+Converter+-+BSS138&qid=1644509232&sr=8-3
  unused pins

custom parts:
  Adafruit 4-channel I2C-safe Bi-directional Logic Level Converter: Because the Arduino (and Basic Stamp) are 5V devices, and most modern sensors, displays, flash cards and modes are 3.3V-only, many makers find that they need to perform level shifting/conversion to protect the 3.3V device from 5V. We do have some other handy level shifters in the shop, from the DIP 74LVC245 to the fancy bi-directional TXB0108. However, neither of these are happy to work with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
  ESP32-38PinWide: Generic 38-Pin ESP32 with wide format (only access to one side of pins on a breadboard) based on Stephen Lilley's HiLetgo ESP-WROOM-32 ESP32 ESP-32S Development Board.
